// Logisim project TSys.circ as structural Verilog: 8 circuits, main circuit main
module main (
  output [7:0] Program_Counter
);

  wire and_1_out, and_2_out, and_3_out, and_4_out, buffer_1_out, buffer_2_out, buffer_3_out, clock_1_out,
       control_1_execute, control_1_fetch, control_1_pc_plus_plus, controlled_buffer_1_out,
       controlled_buffer_2_out, controlled_buffer_3_out, controlled_buffer_7_out, controlled_buffer_8_out,
       controlled_buffer_10_out, controlled_buffer_11_out, decoder_1_out1, decoder_1_out2, decoder_1_out3,
       decoder_1_out4, decoder_1_out5, decoder_1_out6, decoder_1_out7, decoder_1_out8, decoder_1_out9,
       decoder_1_out10, decoder_1_out11, decoder_1_out15, not_1_out, not_2_out, not_3_out, not_4_out,
       or_1_out, or_2_out, or_3_out, or_4_out, or_5_out, or_6_out, programcounter_1_clock_out, TTY;
  wire [2:0] controlled_buffer_4_out;
  wire [3:0] binary_to_bcd_1_p1, binary_to_bcd_1_p3, binary_to_bcd_1_p4, pull_resistor_1_node;
  wire [6:0] controlled_buffer_15_out, numbertoascii_1_output, numbertoascii_2_output, numbertoascii_3_output;
  wire [7:0] acc_2_result, Acc_q, MDR_q, pull_resistor_11_node, ram_1_data;
  wire [11:0] rom_1_data;

  Pull_Resistor pull_resistor_1 (.node(pull_resistor_1_node));
  Decoder #(.select(4), .enable("false")) decoder_1 (
    .out1(decoder_1_out1), .out2(decoder_1_out2), .out3(decoder_1_out3), .out4(decoder_1_out4),
    .out5(decoder_1_out5), .out6(decoder_1_out6), .out7(decoder_1_out7), .out8(decoder_1_out8),
    .out9(decoder_1_out9), .out10(decoder_1_out10), .out11(decoder_1_out11), .out15(decoder_1_out15),
    .sel(pull_resistor_1_node));  // open: out0, out12, out13, out14
  ROM #(.dataWidth(12)) rom_1 (.addr(Program_Counter), .data(rom_1_data));  // open: sel
  Clock clock_1 (.out(clock_1_out));
  or or_1 (or_1_out, control_1_fetch, programcounter_1_clock_out);
  Register MDR (.D(rom_1_data[7:0]), .en(1'b1), .Q(MDR_q), .clk(control_1_fetch));  // open: clr
  Register #(.width(4)) CIR (.D(rom_1_data[11:8]), .Q(pull_resistor_1_node), .clk(control_1_fetch));  // open: en, clr
  or or_2 (or_2_out, decoder_1_out1, decoder_1_out2);
  Control control_1 (
    .Clock(clock_1_out), .Fetch(control_1_fetch), .PC_plus_plus(control_1_pc_plus_plus),
    .Execute(control_1_execute), .Next(or_1_out), .Halt(decoder_1_out15));
  assign controlled_buffer_1_out = control_1_execute ? decoder_1_out1 : 1'bz;  // Controlled_Buffer controlled_buffer_1
  Pull_Resistor pull_resistor_2 (.node(controlled_buffer_1_out));
  assign controlled_buffer_2_out = control_1_execute ? decoder_1_out2 : 1'bz;  // Controlled_Buffer controlled_buffer_2
  assign controlled_buffer_3_out = control_1_execute ? decoder_1_out3 : 1'bz;  // Controlled_Buffer controlled_buffer_3
  assign controlled_buffer_4_out[0] = control_1_execute ? decoder_1_out4 : 1'bz;  // Controlled_Buffer controlled_buffer_4
  assign controlled_buffer_4_out[1] = control_1_execute ? decoder_1_out5 : 1'bz;  // Controlled_Buffer controlled_buffer_5
  assign controlled_buffer_4_out[2] = control_1_execute ? decoder_1_out6 : 1'bz;  // Controlled_Buffer controlled_buffer_6
  assign controlled_buffer_7_out = control_1_execute ? decoder_1_out7 : 1'bz;  // Controlled_Buffer controlled_buffer_7
  Pull_Resistor pull_resistor_3 (.node(controlled_buffer_7_out));
  assign controlled_buffer_8_out = control_1_execute ? decoder_1_out8 : 1'bz;  // Controlled_Buffer controlled_buffer_8
  assign TTY = control_1_execute ? decoder_1_out9 : 1'bz;  // Controlled_Buffer controlled_buffer_9
  assign controlled_buffer_10_out = control_1_execute ? decoder_1_out10 : 1'bz;  // Controlled_Buffer controlled_buffer_10
  assign controlled_buffer_11_out = control_1_execute ? decoder_1_out11 : 1'bz;  // Controlled_Buffer controlled_buffer_11
  or or_3 (or_3_out, decoder_1_out11, decoder_1_out10);
  Pull_Resistor pull_resistor_4 (.node(controlled_buffer_2_out));
  Pull_Resistor pull_resistor_5 (.node(controlled_buffer_3_out));
  Pull_Resistor pull_resistor_6 (.node(controlled_buffer_8_out));
  Pull_Resistor pull_resistor_7 (.node(TTY));
  Pull_Resistor pull_resistor_8 (.node(controlled_buffer_10_out));
  Pull_Resistor pull_resistor_9 (.node(controlled_buffer_11_out));
  ProgramCounter programcounter_1 (
    .MDR(MDR_q), .Acc(acc_2_result), .Jump_type(controlled_buffer_4_out), .Clock(control_1_pc_plus_plus),
    .Clock_out(programcounter_1_clock_out), .PC(Program_Counter));
  or or_4 (or_4_out, controlled_buffer_1_out, controlled_buffer_10_out);
  Pull_Resistor pull_resistor_10 (.node(controlled_buffer_4_out));
  or or_5 (or_5_out, controlled_buffer_2_out, controlled_buffer_11_out);
  Register #(.trigger("high")) Acc (.D(acc_2_result), .en(1'b1), .Q(Acc_q), .clk(1'b1));  // open: clr
  Pull_Resistor pull_resistor_11 (.node(pull_resistor_11_node));
  assign pull_resistor_11_node = or_2_out ? MDR_q : 8'bz;  // Controlled_Buffer controlled_buffer_12
  assign pull_resistor_11_node = or_3_out ? ram_1_data : 8'bz;  // Controlled_Buffer controlled_buffer_13
  Acc acc_2 (
    .ADD(or_4_out), .SUB(or_5_out), .INC(controlled_buffer_3_out), .Result(acc_2_result),
    .Data(pull_resistor_11_node), .Acc(Acc_q));  // open: nil, nil_2
  // Binary_to_BCD binary_to_bcd_1: pin names not known; wires that end beside it: binary_to_bcd_1_p1, Acc_q, binary_to_bcd_1_p3, binary_to_bcd_1_p4
  assign acc_2_result = controlled_buffer_7_out ? ram_1_data : 8'bz;  // Controlled_Buffer controlled_buffer_14
  not not_1 (not_1_out, TTY);
  buf buffer_1 (buffer_1_out, and_1_out);
  not not_2 (not_2_out, buffer_1_out);
  buf buffer_2 (buffer_2_out, and_2_out);
  not not_3 (not_3_out, buffer_2_out);
  buf buffer_3 (buffer_3_out, and_3_out);
  not not_4 (not_4_out, buffer_3_out);
  NumberToAscii numbertoascii_1 (.in_1(binary_to_bcd_1_p1), .Output(numbertoascii_1_output));
  NumberToAscii numbertoascii_2 (.in_1(binary_to_bcd_1_p3), .Output(numbertoascii_2_output));
  NumberToAscii numbertoascii_3 (.in_1(binary_to_bcd_1_p4), .Output(numbertoascii_3_output));
  // Binary_to_BCD binary_to_bcd_2: pin names not known; wires that end beside it: Acc_q
  assign controlled_buffer_15_out = and_1_out ? numbertoascii_1_output : 7'bz;  // Controlled_Buffer controlled_buffer_15
  and and_1 (and_1_out, TTY, not_1_out);
  assign controlled_buffer_15_out = and_2_out ? numbertoascii_2_output : 7'bz;  // Controlled_Buffer controlled_buffer_16
  and and_2 (and_2_out, buffer_1_out, not_2_out);
  and and_3 (and_3_out, buffer_2_out, not_3_out);
  and and_4 (and_4_out, buffer_3_out, not_4_out);
  Hex_Digit_Display hex_digit_display_1 ();  // open: value, dp
  Hex_Digit_Display hex_digit_display_2 ();  // open: value, dp
  RAM #(.bus("separate")) ram_1 (
    .addr(MDR_q), .din(Acc_q), .data(ram_1_data), .clk(controlled_buffer_8_out));  // open: str, sel, ld, clr
  assign controlled_buffer_15_out = and_3_out ? numbertoascii_3_output : 7'bz;  // Controlled_Buffer controlled_buffer_17
  TTY tty_1 (.data(controlled_buffer_15_out), .clk(or_6_out), .we(1'b1));  // open: clr
  assign controlled_buffer_15_out = and_4_out ? 7'b0001101 : 7'bz;  // Controlled_Buffer controlled_buffer_18
  Hex_Digit_Display hex_digit_display_3 ();  // open: value, dp
  or or_6 (or_6_out, and_3_out, and_2_out, and_1_out, and_4_out);

  // Notes on the sheet:
  //   Program
  //   contents of rom_1 (hex, n*v repeats v):
  //   700 900 101 900 900 800 801 700 a01 900 800 701 a00 900 801 407
  //   Working Memory
  //   Accumulator
endmodule

// ALU
module Acc (
  input  SUB,
  input  ADD,
  input  INC,
  input  nil,
  input  nil_2,
  input  [7:0] Acc,
  input  [7:0] Data,
  output [7:0] Result
);

  wire and_1_out, buffer_1_out, buffer_2_out, buffer_3_out, buffer_4_out, buffer_5_out, buffer_6_out,
       not_1_out, or_1_out;
  wire [7:0] adder_1_out, adder_2_out, controlled_buffer_1_out, controlled_buffer_2_out,
       controlled_buffer_3_out, or_2_out, subtractor_1_out;

  buf buffer_1 (buffer_1_out, SUB);
  buf buffer_2 (buffer_2_out, buffer_1_out);
  buf buffer_3 (buffer_3_out, buffer_2_out);
  buf buffer_4 (buffer_4_out, ADD);
  buf buffer_5 (buffer_5_out, buffer_3_out);
  Adder adder_1 (.a(Acc), .b(Data), .out(adder_1_out));  // open: cin, cout
  Subtractor subtractor_1 (.a(Acc), .b(Data), .out(subtractor_1_out));  // open: bin, bout
  Adder adder_2 (.a(Acc), .b(8'h1), .out(adder_2_out));  // open: cin, cout
  buf buffer_6 (buffer_6_out, INC);
  assign controlled_buffer_1_out = buffer_4_out ? adder_1_out : 8'bz;  // Controlled_Buffer controlled_buffer_1
  assign controlled_buffer_2_out = buffer_5_out ? subtractor_1_out : 8'bz;  // Controlled_Buffer controlled_buffer_2
  assign controlled_buffer_3_out = buffer_6_out ? adder_2_out : 8'bz;  // Controlled_Buffer controlled_buffer_3
  Pull_Resistor pull_resistor_1 (.node(controlled_buffer_1_out));
  Pull_Resistor pull_resistor_2 (.node(controlled_buffer_2_out));
  Pull_Resistor pull_resistor_3 (.node(controlled_buffer_3_out));
  or or_1 (or_1_out, buffer_6_out, buffer_5_out, buffer_4_out);
  assign or_2_out = controlled_buffer_1_out | controlled_buffer_2_out | controlled_buffer_3_out;  // OR_Gate or_2, 8 bits wide
  and and_1 (and_1_out, or_1_out, not_1_out);
  not not_1 (not_1_out, or_1_out);
  assign Result = and_1_out ? or_2_out : 8'bz;  // Controlled_Buffer controlled_buffer_4
endmodule

// Z
module Is0 (
  input  [7:0] Input,
  output out_2
);

  nor nor_1 (out_2, Input[0], Input[1], Input[2], Input[3], Input[4], Input[5], Input[6], Input[7]);
endmodule

// +
module NotNegative (
  input  [7:0] Input,
  output out_2
);

  not not_1 (out_2, Input[7]);
endmodule

// PC
module ProgramCounter (
  input  Clock,
  input  [7:0] MDR,
  input  [7:0] Acc,
  input  [2:0] Jump_type,
  output [7:0] PC,
  output Clock_out
);

  wire _0_2_out_2, _0_out_2, and_1_out, and_2_out, and_3_out, buffer_1_out, buffer_2_out, not_1_out,
       not_2_out, not_3_out, or_1_out, or_2_out;
  wire [7:0] adder_1_out, controlled_buffer_1_out;

  NotNegative _0 (.Input(Acc), .out_2(_0_out_2));
  Is0 _0_2 (.Input(Acc), .out_2(_0_2_out_2));
  not not_1 (not_1_out, Clock);
  and and_1 (and_1_out, _0_out_2, Jump_type[2]);
  and and_2 (and_2_out, _0_2_out_2, Jump_type[1]);
  and and_3 (and_3_out, Clock, not_1_out);
  assign controlled_buffer_1_out = buffer_1_out ? MDR : 8'bz;  // Controlled_Buffer controlled_buffer_1
  buf buffer_1 (buffer_1_out, or_1_out);
  or or_1 (or_1_out, and_1_out, and_2_out, Jump_type[0]);
  Register u_PC (.D(controlled_buffer_1_out), .en(1'b1), .Q(PC), .clk(or_2_out));  // open: clr
  buf buffer_2 (buffer_2_out, or_1_out);
  or or_2 (or_2_out, and_3_out, buffer_2_out);
  assign controlled_buffer_1_out = not_2_out ? adder_1_out : 8'bz;  // Controlled_Buffer controlled_buffer_2
  not not_2 (not_2_out, or_1_out);
  assign Clock_out = not_3_out ? or_2_out : 1'bz;  // Controlled_Buffer controlled_buffer_3
  Pull_Resistor pull_resistor_1 (.node(Clock_out));
  not not_3 (not_3_out, or_1_out);
  Adder adder_1 (.a(PC), .b(8'h1), .out(adder_1_out));  // open: cin, cout

  // Notes on the sheet:
  //   0: Always
  //   1: If Zero
  //   2: If positive
endmodule

// CTRL
module Control (
  input  Next,
  input  Clock,
  input  Halt,
  output Fetch,
  output PC_plus_plus,
  output Execute
);

  wire and_1_out, and_2_out, and_3_out, controlled_buffer_1_out, not_1_out, not_2_out, not_3_out, not_4_out,
       not_5_out, not_6_out, not_7_out, not_8_out, s_r_ff_1_q, s_r_ff_2_q, s_r_ff_3_q, s_r_ff_4_q;

  not not_1 (not_1_out, Next);
  and and_1 (and_1_out, not_1_out, Next);
  assign controlled_buffer_1_out = not_2_out ? Clock : 1'bz;  // Controlled_Buffer controlled_buffer_1
  and and_2 (and_2_out, s_r_ff_1_q, and_1_out);
  and and_3 (and_3_out, s_r_ff_2_q, and_1_out);
  not not_2 (not_2_out, s_r_ff_4_q);
  S_R_Flip_Flop #(.trigger("high")) s_r_ff_1 (
    .S(controlled_buffer_1_out), .clk(1'b1), .R(not_3_out), .Q(s_r_ff_1_q), .en(1'b1));  // open: Qn, preset, reset
  not not_3 (not_3_out, controlled_buffer_1_out);
  S_R_Flip_Flop #(.trigger("high")) s_r_ff_2 (
    .S(and_2_out), .clk(1'b1), .R(not_4_out), .Q(s_r_ff_2_q), .en(1'b1));  // open: Qn, preset, reset
  not not_4 (not_4_out, controlled_buffer_1_out);
  S_R_Flip_Flop #(.trigger("high")) s_r_ff_3 (
    .S(and_3_out), .clk(1'b1), .R(not_5_out), .Q(s_r_ff_3_q));  // open: Qn, preset, reset, en
  not not_5 (not_5_out, controlled_buffer_1_out);
  S_R_Flip_Flop s_r_ff_4 (.S(Halt), .Q(s_r_ff_4_q));  // open: clk, R, Qn, preset, reset, en
  not not_6 (not_6_out, s_r_ff_1_q);
  not not_7 (not_7_out, s_r_ff_2_q);
  not not_8 (not_8_out, s_r_ff_3_q);
  and and_4 (Fetch, s_r_ff_1_q, not_6_out);
  and and_5 (PC_plus_plus, s_r_ff_2_q, not_7_out);
  and and_6 (Execute, s_r_ff_3_q, not_8_out);
endmodule

module SR_Latch (
  input  in_1,
  input  in_2,
  input  in_3,
  input  in_4,
  input  Data,
  input  Enable,
  input  Data_2,
  output out_8,
  output Q,
  output nQ,
  output out_11,
  output Q_2,
  output out_13,
  output out_14
);

  wire button_1_out, nand_1_out, nand_2_out, nand_3_out, nand_4_out, nand_5_out, nand_6_out, nand_7_out,
       nand_8_out, nand_10_out, nand_12_out, nand_14_out, nand_16_out, nand_17_out, nand_18_out, nand_21_out,
       nand_22_out, nand_23_out, nand_24_out, not_1_out, not_2_out, not_3_out, not_4_out;

  Button button_1 (.out(button_1_out));
  nand nand_1 (nand_1_out, in_1, button_1_out);
  nand nand_2 (nand_2_out, button_1_out, not_1_out);
  not not_1 (not_1_out, in_1);
  nand nand_3 (nand_3_out, in_2, button_1_out);
  nand nand_4 (nand_4_out, button_1_out, not_2_out);
  not not_2 (not_2_out, in_2);
  nand nand_5 (nand_5_out, in_3, button_1_out);
  nand nand_6 (nand_6_out, button_1_out, not_3_out);
  not not_3 (not_3_out, in_3);
  nand nand_7 (nand_7_out, in_4, button_1_out);
  nand nand_8 (nand_8_out, button_1_out, not_4_out);
  not not_4 (not_4_out, in_4);
  nand nand_9 (out_8, nand_1_out, nand_10_out);
  nand nand_10 (nand_10_out, out_8, nand_2_out);
  nand nand_11 (out_11, nand_3_out, nand_12_out);
  nand nand_12 (nand_12_out, out_11, nand_4_out);
  nand nand_13 (out_13, nand_5_out, nand_14_out);
  nand nand_14 (nand_14_out, out_13, nand_6_out);
  nand nand_15 (out_14, nand_7_out, nand_16_out);
  nand nand_16 (nand_16_out, out_14, nand_8_out);
  nand nand_17 (nand_17_out, Data, Enable);
  nand nand_18 (nand_18_out, Enable, ~Data);  // NAND_Gate
  nand nand_19 (Q, nand_17_out, nQ);
  nand nand_20 (nQ, Q, nand_18_out);
  nand nand_21 (nand_21_out, Data_2, 1'b1);
  nand nand_22 (nand_22_out, nand_21_out, nand_23_out);
  nand nand_23 (nand_23_out, nand_22_out, nand_24_out);
  nand nand_24 (nand_24_out, 1'b1, ~Data_2);  // NAND_Gate
  Pull_Resistor pull_resistor_1 (.node(Q_2));
  assign Q_2 = nand_23_out ? nand_22_out : 1'bz;  // Controlled_Buffer controlled_buffer_1
endmodule

// N2A
module NumberToAscii (
  input  [3:0] in_1,
  output [6:0] Output
);

  Pull_Resistor pull_resistor_1 (.node(in_1));

  assign Output = {3'b011, in_1};
endmodule
